# Fritzing sketch kupattahupetis (saved by Fritzing 0.9.3b)

parts:
  KY-1 = Keyes Relay [package=THT]
  Part1 = Arduino Uno (Rev3)
  Power_plug1 = Power plug

nets:
  N1: KY-1.signal, Part1.D7
  N2: KY-1.power, Part1.5V
  N3: KY-1.ground, Part1.GND
  N4: KY-1.NC, KY-1.NO, Power_plug1.VCC

notes:
  relay pin 7
  Colokan 220V
  ke pompa air

custom parts:
  Keyes Relay: The Keyes 5V relay module is suitable for SCM development, home appliance control. It uses a 5V~12V TIL control signal which can control DC / AC signal.
